# Fritzing sketch BMP180_I2Clcd_UNO (saved by Fritzing 0.8.7b)
breadboards: 1

parts:
  U1 = LCD-16X2 [package=lcd-16x2]
  Part1 = Arduino Uno (Rev3) - ICSP
  LCM1602_IIC1 = LCM1602 IIC [part_number="LCM1602 IIC" chip_label="LCM1602 IIC" package="DIP (Dual Inline) [THT]"]
  Part2 = Adafruit BMP180

nets:
  VSS: U1.VSS, LCM1602_IIC1.VSS
  VDD: U1.VDD, LCM1602_IIC1.VDD
  N1: U1.VO, LCM1602_IIC1.V0
  N2: U1.RS, LCM1602_IIC1.RS
  N3: U1.R_W, LCM1602_IIC1.RW
  N4: U1.E, LCM1602_IIC1.E
  N5: U1.DB0, LCM1602_IIC1.D0
  N6: U1.DB1, LCM1602_IIC1.D1
  N7: U1.DB2, LCM1602_IIC1.D2
  N8: U1.DB3, LCM1602_IIC1.D3
  N9: U1.DB4, LCM1602_IIC1.D4
  N10: U1.DB5, LCM1602_IIC1.D5
  N11: U1.DB6, LCM1602_IIC1.D6
  N12: U1.DB7, LCM1602_IIC1.D7
  N13: U1.A, LCM1602_IIC1.A
  N14: U1.K, LCM1602_IIC1.K
  N15: Part1.A4/SDA, LCM1602_IIC1.SDA, Part2.SDA
  N16: Part1.A5/SCL, LCM1602_IIC1.SCL, Part2.SCL
  5V: Part1.5V, LCM1602_IIC1.VCC, Part2.+3V3
  GND: Part1.GND, LCM1602_IIC1.GND, Part2.GND

notes:
  Sensor/ Breakout ---------> Arduino
  VCC ------------------> 5V
  Gnd ------------------> Ground
  SDA ------------------> A4 (Analog No.4)
  SCL -------------------> A5 (Analog No.5)

custom parts:
  LCM1602 IIC: I2C-Module to use a 1602 or 2004 LCD on with the wire.h libory Serial LCD Modul
  Adafruit BMP180: This precision sensor from Bosch is the best low-cost sensing solution for measuring barometric pressure and temperature. Because pressure changes with altitude you can also use it as an altimeter! The sensor is soldered onto a PCB with a 3.3V regulator, I2C level shifter and pull-up resistors on the I2C pins. The BMP180 is the next-generation of sensors from Bosch, and replaces the BMP085.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
