# Fritzing sketch ESP01 BMP180 THINGSPEAK (saved by Fritzing 0.8.7b)

parts:
  Mod1 = Arduino Sensor Shield v5.0
  M2 = ESP-01 Breakout Board Breadboard Adapter [part_number=ESP8266]
  Part2 = Adafruit BMP180  # not connected
  Part3 = Adafruit BMP180  # not connected
  Part4 = Adafruit BMP180

nets:
  N1: Mod1.SD-D11, Mod1.11-S, Mod1.ParallelLCD-D11, M2.TXD, M2.VCC
  N2: Mod1.SD-D13, Mod1.ParallelLCD-D13, M2.GND
  N3: Mod1.A4-SIG, Mod1.IIC-SDA, Part4.SDA
  N4: Mod1.A5-SIG, Mod1.IIC-SCL, Part4.SCL
  N5: Mod1.IIC-GND, Mod1.ParallelLCD-GND, Part4.GND
  N6: Mod1.IIC-VCC, Mod1.ParallelLCD-VCC, Part4.+5V
  N7: Mod1.10-S, Mod1.ParallelLCD-D10, M2.RXD

custom parts:
  Arduino Sensor Shield v5.0: Arduino Sensor Shield v5.0 provides I2C interface, Bluetooth module communication interface, SD card module communication interface, APC220 wireless RF modules communication interface, RB URF V1.1 ultrasonic sensors interface, 12864 LCD serial and parallel interface, 32 servo controller interfaces. In addition (with the sel jumper removed) allows an external power supply for the servos as the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
  ESP-01 Breakout Board Breadboard Adapter: Generic WiFi Module based on the ESP8266 with onboard PCB antenna and UART communications with breadboard friendly breakout board attached.
  Adafruit BMP180: This precision sensor from Bosch is the best low-cost sensing solution for measuring barometric pressure and temperature. Because pressure changes with altitude you can also use it as an altimeter! The sensor is soldered onto a PCB with a 3.3V regulator, I2C level shifter and pull-up resistors on the I2C pins. The BMP180 is the next-generation of sensors from Bosch, and replaces the BMP085.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
