# Fritzing sketch MAX30100 LCD (saved by Fritzing 0.8.7b)

parts:
  Componente1 = Arduino Uno (Rev3)
  Convertitore_Expander_seriale = LCM1602 IIC [chip_label="Modulo " part_number="LCM1602 IIC" package="DIP (Dual Inline) [THT]"]
  M2 = MAX30102
  Display_LCD_16x2 = LCD Display 16x2

nets:
  N1: Componente1.A4/SDA, Convertitore_Expander_seriale.SDA, M2.SDA
  N2: Componente1.A5/SCL, Convertitore_Expander_seriale.SCL, M2.SCL
  5V: Componente1.5V, M2.VIN
  GND: Componente1.GND, M2.GND
  N3: Convertitore_Expander_seriale.VSS, Display_LCD_16x2.aún_sin_nombre#0
  N4: Convertitore_Expander_seriale.VDD, Display_LCD_16x2.aún_sin_nombre#1
  N5: Convertitore_Expander_seriale.V0, Display_LCD_16x2.aún_sin_nombre#2
  N6: Convertitore_Expander_seriale.RS, Display_LCD_16x2.aún_sin_nombre#3
  N7: Convertitore_Expander_seriale.RW, Display_LCD_16x2.aún_sin_nombre#4
  N8: Convertitore_Expander_seriale.E, Display_LCD_16x2.aún_sin_nombre#5
  N9: Convertitore_Expander_seriale.D0, Display_LCD_16x2.aún_sin_nombre#6
  N10: Convertitore_Expander_seriale.D1, Display_LCD_16x2.aún_sin_nombre#7
  N11: Convertitore_Expander_seriale.D2, Display_LCD_16x2.aún_sin_nombre#8
  N12: Convertitore_Expander_seriale.D3, Display_LCD_16x2.aún_sin_nombre#9
  N13: Convertitore_Expander_seriale.D4, Display_LCD_16x2.aún_sin_nombre#10
  N14: Convertitore_Expander_seriale.D5, Display_LCD_16x2.aún_sin_nombre#11
  N15: Convertitore_Expander_seriale.D6, Display_LCD_16x2.aún_sin_nombre#12
  N16: Convertitore_Expander_seriale.D7, Display_LCD_16x2.aún_sin_nombre#13
  N17: Convertitore_Expander_seriale.A, Display_LCD_16x2.aún_sin_nombre#14
  N18: Convertitore_Expander_seriale.K, Display_LCD_16x2.aún_sin_nombre#15
  N19: Convertitore_Expander_seriale.LED_A, Convertitore_Expander_seriale.LED_B

custom parts:
  LCM1602 IIC: I2C-Module to use a 1602 or 2004 LCD on with the wire.h libory Serial LCD Modul
  MAX30102: Oximeter module using the MAX30102 chip. You may wish to read (and check your module) this post on power problems with these modules: https://reedpaper.wordpress.com/2018/08/22/pulse-oximeter-max30100-max30102-how-to-fix-wrong-board/ . As usual, if you want the mounting holes in pcb, you need to drag a hole over the pad in silkscreen to actually drill the hole (by default they are not drilled)
