# Fritzing sketch DS1302_RTC_LCD_SD_MX30100 (saved by Fritzing 0.8.7b)

parts:
  Componente1 = Arduino Uno (Rev3)
  Convertitore_Expander_seriale = LCM1602 IIC [chip_label="Modulo " part_number="LCM1602 IIC" package="DIP (Dual Inline) [THT]"]
  MH-Real-Time_Clock_Module_2 = RTC_DS1302_module
  M2 = MAX30102
  SD_card_module1 = SD Card Module
  Display_LCD_16x2 = LCD Display 16x2

nets:
  N1: Componente1.A4/SDA, Convertitore_Expander_seriale.SDA, M2.SDA
  N2: Componente1.A5/SCL, Convertitore_Expander_seriale.SCL, M2.SCL
  N3: Componente1.D10_PWM/SS, SD_card_module1.CS
  N4: Componente1.D11_PWM/MOSI, SD_card_module1.MOSI
  N5: Componente1.D12/MISO, SD_card_module1.MISO
  N6: Componente1.D13/SCK, SD_card_module1.SCK
  GND: Componente1.GND, M2.GND, SD_card_module1.GND
  N7: Componente1.D2, MH-Real-Time_Clock_Module_2.RST
  N8: Componente1.D4, MH-Real-Time_Clock_Module_2.DAT
  N9: Componente1.D5_PWM, MH-Real-Time_Clock_Module_2.CLK
  5V: Componente1.5V, M2.VIN, SD_card_module1.+5
  N10: Convertitore_Expander_seriale.VSS, Display_LCD_16x2.aún_sin_nombre#0
  N11: Convertitore_Expander_seriale.VDD, Display_LCD_16x2.aún_sin_nombre#1
  N12: Convertitore_Expander_seriale.V0, Display_LCD_16x2.aún_sin_nombre#2
  N13: Convertitore_Expander_seriale.RS, Display_LCD_16x2.aún_sin_nombre#3
  N14: Convertitore_Expander_seriale.RW, Display_LCD_16x2.aún_sin_nombre#4
  N15: Convertitore_Expander_seriale.E, Display_LCD_16x2.aún_sin_nombre#5
  N16: Convertitore_Expander_seriale.D0, Display_LCD_16x2.aún_sin_nombre#6
  N17: Convertitore_Expander_seriale.D1, Display_LCD_16x2.aún_sin_nombre#7
  N18: Convertitore_Expander_seriale.D2, Display_LCD_16x2.aún_sin_nombre#8
  N19: Convertitore_Expander_seriale.D3, Display_LCD_16x2.aún_sin_nombre#9
  N20: Convertitore_Expander_seriale.D4, Display_LCD_16x2.aún_sin_nombre#10
  N21: Convertitore_Expander_seriale.D5, Display_LCD_16x2.aún_sin_nombre#11
  N22: Convertitore_Expander_seriale.D6, Display_LCD_16x2.aún_sin_nombre#12
  N23: Convertitore_Expander_seriale.D7, Display_LCD_16x2.aún_sin_nombre#13
  N24: Convertitore_Expander_seriale.A, Display_LCD_16x2.aún_sin_nombre#14
  N25: Convertitore_Expander_seriale.K, Display_LCD_16x2.aún_sin_nombre#15
  GND_2: Convertitore_Expander_seriale.GND, MH-Real-Time_Clock_Module_2.GND
  VCC: Convertitore_Expander_seriale.VCC, MH-Real-Time_Clock_Module_2.VCC
  N26: Convertitore_Expander_seriale.LED_A, Convertitore_Expander_seriale.LED_B

notes:
  Test modulo MH-Real-Time Clock Module 2
  by ismailsa
  Youtube: http://youtube.com/c/kajidataonline

custom parts:
  LCM1602 IIC: I2C-Module to use a 1602 or 2004 LCD on with the wire.h libory Serial LCD Modul
  RTC_DS1302_module: Arduino module DS1302 SPI Real Time Clock
  MAX30102: Oximeter module using the MAX30102 chip. You may wish to read (and check your module) this post on power problems with these modules: https://reedpaper.wordpress.com/2018/08/22/pulse-oximeter-max30100-max30102-how-to-fix-wrong-board/ . As usual, if you want the mounting holes in pcb, you need to drag a hole over the pad in silkscreen to actually drill the hole (by default they are not drilled)
  SD Card Module: SD Card Module Slot Socket Reader For Arduino ARM MCU
