# Fritzing sketch WEMOS_BMP_LCD (saved by Fritzing 0.8.7b)
breadboards: 1

parts:
  WeMos_D1_R2 = WeMos D1 R2
  Display_LCD_16x3 = LCD Display 16x2
  Convertitore_Expander_seriale1 = LCM1602 IIC [chip_label="Modulo " part_number="LCM1602 IIC" package="DIP (Dual Inline) [THT]"]
  Part1 = Adafruit BMP180

nets:
  N1: WeMos_D1_R2.D14, Convertitore_Expander_seriale1.SDA, Part1.SDA
  N2: WeMos_D1_R2.D15, Convertitore_Expander_seriale1.SCL, Part1.SCL
  GND: WeMos_D1_R2.GND, Convertitore_Expander_seriale1.GND, Part1.GND
  5V: WeMos_D1_R2.5V, Convertitore_Expander_seriale1.VCC, Part1.+3V3
  N3: Display_LCD_16x3.aún_sin_nombre#0, Convertitore_Expander_seriale1.VSS
  N4: Display_LCD_16x3.aún_sin_nombre#1, Convertitore_Expander_seriale1.VDD
  N5: Display_LCD_16x3.aún_sin_nombre#2, Convertitore_Expander_seriale1.V0
  N6: Display_LCD_16x3.aún_sin_nombre#3, Convertitore_Expander_seriale1.RS
  N7: Display_LCD_16x3.aún_sin_nombre#4, Convertitore_Expander_seriale1.RW
  N8: Display_LCD_16x3.aún_sin_nombre#5, Convertitore_Expander_seriale1.E
  N9: Display_LCD_16x3.aún_sin_nombre#6, Convertitore_Expander_seriale1.D0
  N10: Display_LCD_16x3.aún_sin_nombre#7, Convertitore_Expander_seriale1.D1
  N11: Display_LCD_16x3.aún_sin_nombre#8, Convertitore_Expander_seriale1.D2
  N12: Display_LCD_16x3.aún_sin_nombre#9, Convertitore_Expander_seriale1.D3
  N13: Display_LCD_16x3.aún_sin_nombre#10, Convertitore_Expander_seriale1.D4
  N14: Display_LCD_16x3.aún_sin_nombre#11, Convertitore_Expander_seriale1.D5
  N15: Display_LCD_16x3.aún_sin_nombre#12, Convertitore_Expander_seriale1.D6
  N16: Display_LCD_16x3.aún_sin_nombre#13, Convertitore_Expander_seriale1.D7
  N17: Display_LCD_16x3.aún_sin_nombre#14, Convertitore_Expander_seriale1.A
  N18: Display_LCD_16x3.aún_sin_nombre#15, Convertitore_Expander_seriale1.K
  N19: Convertitore_Expander_seriale1.LED_A, Convertitore_Expander_seriale1.LED_B

custom parts:
  WeMos D1 R2: The D1 R2 is a mini wifi board based on the ESP-8266EX.
  LCM1602 IIC: I2C-Module to use a 1602 or 2004 LCD on with the wire.h libory Serial LCD Modul
  Adafruit BMP180: This precision sensor from Bosch is the best low-cost sensing solution for measuring barometric pressure and temperature. Because pressure changes with altitude you can also use it as an altimeter! The sensor is soldered onto a PCB with a 3.3V regulator, I2C level shifter and pull-up resistors on the I2C pins. The BMP180 is the next-generation of sensors from Bosch, and replaces the BMP085.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
